# Fritzing sketch Angle meter MPU6050 (saved by Fritzing 0.9.3b)
circuit board: 8.46667cm x 5.64444cm

parts:
  Arduino_Nano_AT328P = Arduino Nano (Rev3.0)
  Function_SW = SWITCH-MOMENTARY-2 [package=tactile-pth-12mm]
  LIPO_or_LI-ION = LIPO-2000mAh [package=lipo-2000]
  ON/OFF_switch = Taiway 100-SP-X-T1 SPDT Miniature Toggle Switch [part_number=100-SP-X-T1-0-0-B1-M1 package=THT]
  MPU-1 = Adafruit MPU6050
  Composant1 = Adafruit 1.3in 240x240 IPS TFT [part_number="Adafruit #4313"]

nets:
  GND: Arduino_Nano_AT328P.GND, Function_SW.2, LIPO_or_LI-ION.-, MPU-1.GND, Composant1.GND
  N1: Arduino_Nano_AT328P.D2, Function_SW.1
  N2: Arduino_Nano_AT328P.D7, Composant1.TFTDC
  N3: Arduino_Nano_AT328P.D8, Composant1.RESET
  N4: Arduino_Nano_AT328P.D11/MOSI, Composant1.MOSI
  N5: Arduino_Nano_AT328P.VIN, ON/OFF_switch.COM
  5V: Arduino_Nano_AT328P.5V, MPU-1.VCC
  N6: Arduino_Nano_AT328P.A5, MPU-1.SCL
  N7: Arduino_Nano_AT328P.A4, MPU-1.SDA
  3V3: Arduino_Nano_AT328P.3V3, Composant1.VIN, Composant1.+3V3
  N8: Arduino_Nano_AT328P.D13/SCK, Composant1.SCK
  N9: LIPO_or_LI-ION.+, ON/OFF_switch.L2

custom parts:
  Adafruit MPU6050: The MPU-6050 is a popular six axis accelerometer and gyroscope (gyro) that has all the info you need on how things are shakin' and spinnin' . With six axes of sensing and 16-bit measurements, you'll have everything you need to give your robot friend an inner ear. This combination of gyroscopes and accelerometers is commonly referred to as an Inertial Measurement Unit or IMU. Not so long ago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
  Adafruit 1.3in 240x240 IPS TFT: We've been looking for a display like this for a long time - it's so small only 1.3" diagonal but has a high density 260 ppi, 240x240 pixel display with full-angle viewing. It looks a lot like our 1.44" 128x128 display, but has 4x as many pixels and looks great at any angle. We've seen displays of this caliber used in smartwatches and small electronic devices but they've always been MIPI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
